# Fritzing sketch Sketch2 (saved by Fritzing 0.9.3b)
breadboards: 1

parts:
  Raspberry_Pi_B_rev1 = Raspberry Pi B rev2
  IC1 = IC, DIP package, 14 pins [chip_label=74AHC125]
  Power_plug_5V = Power plug
  LED_Strip = mystery part, 3 pins [chip_label=?]
  USB-Plug = USB_MICROB_PLUG [package=micro-b-ra-th]

nets:
  N1: Raspberry_Pi_B_rev1.GPIO_18, IC1.pin2
  GND: IC1.pin1, IC1.pin7, Power_plug_5V.GND, LED_Strip.pin3, USB-Plug.GND
  N2: IC1.pin3, LED_Strip.pin2
  VCC: IC1.pin14, Power_plug_5V.VCC, LED_Strip.pin1, USB-Plug.VCC
